# Fritzing sketch pulse_counter_ESP8266 (saved by Fritzing 0.9.2b)
breadboards: 1

parts:
  U1 = NodeMCU V1.0
  R1 = Resistor [tolerance=±5% resistance=1k package=THT]
  LED1 = LED - 5mm [color="Red (633nm)" package="5 mm [THT]"]
  R2 = Resistor [tolerance=±5% resistance=10k package=THT]
  S1 = Reed switch [part_number=Reed package=THT]

nets:
  N1: U1.D1, R2.Pin_0, S1.pin_1
  N2: U1.D2, R1.Pin_0
  N3: U1.GND, LED1.cathode, R2.Pin_1
  N4: U1.Vin, S1.pin_2
  N5: R1.Pin_1, LED1.anode

custom parts:
  NodeMCU V1.0: ESP8266 based NodeMCU
